# Fritzing sketch sonar (saved by Fritzing 0.9.3b)
breadboards: 1

parts:
  LED1 = LED - 5mm [color="Green (555nm)" package="5 mm [THT]"]
  R3 = Resistor [tolerance=±5% resistance=220 package=THT]
  Part2 = SRF05 Ultrasonic Rangefinder
  Part3 = Arduino Uno (Rev3)
  LED2 = LED - 5mm [color="Red (633nm)" package="5 mm [THT]"]
  R4 = Resistor [tolerance=±5% resistance=220 package=THT]
  R5 = TRIMPOT [package=3362u-2]

nets:
  N1: LED1.cathode, R3.Pin_0
  N2: LED1.anode, Part3.D6_PWM
  GND: R3.Pin_1, Part2.GND, Part3.GND, R4.Pin_1, R5.CW
  VCC: Part2.VCC, Part3.5V, R5.CCW
  N3: Part2.Trig, Part3.D12/MISO
  N4: Part2.Echo, Part3.D11_PWM/MOSI
  N5: Part3.A0, R5.WIPER
  N6: Part3.D7, LED2.anode
  N7: LED2.cathode, R4.Pin_0
